// Logisim project MIPS.circ as structural Verilog
module ALU_8_bit (
  input  [7:0] In1,
  input  [7:0] In2,
  input  [2:0] AluOp,
  input  [3:0] ShAmt,
  output [7:0] out_5,
  output IsEqual
);

  wire and_2_out, comparator_1_eq;
  wire [7:0] adder_1_out, and_1_out, not_1_out, or_1_out, subtractor_1_out;
  wire [15:0] bit_extender_1_out, bit_extender_2_out, shifter_1_out, shifter_2_out;

  assign bit_extender_1_out = {{8{In1[7]}}, In1};  // Bit_Extender bit_extender_1
  assign bit_extender_2_out = {{8{In1[7]}}, In1};  // Bit_Extender bit_extender_2
  Adder adder_1 (.a(In1), .b(In2), .out(adder_1_out), .cin(1'b0));  // open: cout
  Subtractor subtractor_1 (.a(In1), .b(In2), .out(subtractor_1_out), .bin(1'b0));  // open: bout
  assign and_1_out = In1 & In2;  // AND_Gate and_1, 8 bits wide
  assign or_1_out = In1 | In2;  // OR_Gate or_1, 8 bits wide
  assign not_1_out = ~or_1_out;  // NOT_Gate not_1, 8 bits wide
  Shifter #(.width(16)) shifter_1 (.in(bit_extender_1_out), .\dist (ShAmt), .out(shifter_1_out));
  Shifter #(.width(16), .shift("lr")) shifter_2 (.in(bit_extender_2_out), .\dist (ShAmt), .out(shifter_2_out));
  Comparator comparator_1 (.a(In1), .b(In2), .eq(comparator_1_eq));  // open: gt, lt
  Multiplexer #(.select(3), .width(8), .enable("false")) multiplexer_1 (
    .in0(adder_1_out), .in1(subtractor_1_out), .in2(and_1_out), .in3(or_1_out), .in4(not_1_out),
    .in5(shifter_1_out[7:0]), .in6(shifter_2_out[7:0]), .in7({8{1'b0}}), .out(out_5), .sel(AluOp));
  and and_2 (and_2_out, AluOp[0], AluOp[1], AluOp[2]);
  xor xor_1 (IsEqual, and_2_out, comparator_1_eq);

  // Notes on the sheet:
  //   Alu Operations:
  //   0 = ADD
  //   1 = SUB
  //   2 = AND
  //   3 = OR
  //   4 = NOR
  //   5 = SLL
  //   6 = SRL
  //   7 = BNE
endmodule

module Registers (
  input  [3:0] RS,
  input  [3:0] RT,
  input  [7:0] WriteData,
  input  RegWrite,
  input  CLK,
  input  [3:0] RD,
  output [7:0] ReadData1,
  output [7:0] ReadData2
);

  wire and_1_out, demultiplexer_1_out0, demultiplexer_1_out1, demultiplexer_1_out2, demultiplexer_1_out3,
       demultiplexer_1_out4, demultiplexer_1_out5, demultiplexer_1_out6;
  wire [7:0] sp_q, t0_q, t1_q, t2_q, t3_q, t4_q, zero_q;

  and and_1 (and_1_out, RegWrite, CLK);
  Demultiplexer #(.select(3), .enable("false")) demultiplexer_1 (
    .out0(demultiplexer_1_out0), .out1(demultiplexer_1_out1), .out2(demultiplexer_1_out2),
    .out3(demultiplexer_1_out3), .out4(demultiplexer_1_out4), .out5(demultiplexer_1_out5),
    .out6(demultiplexer_1_out6), .in(and_1_out), .sel(RD[2:0]));  // open: out7
  Register t0 (.D(WriteData), .Q(t0_q), .clk(demultiplexer_1_out1));  // open: en, clr
  Register zero (.D({8{1'b0}}), .Q(zero_q), .clk(demultiplexer_1_out0));  // open: en, clr
  Register t1 (.D(WriteData), .Q(t1_q), .clk(demultiplexer_1_out2));  // open: en, clr
  Register t2 (.D(WriteData), .Q(t2_q), .clk(demultiplexer_1_out3));  // open: en, clr
  Register t3 (.D(WriteData), .Q(t3_q), .clk(demultiplexer_1_out4));  // open: en, clr
  Register t4 (.D(WriteData), .Q(t4_q), .clk(demultiplexer_1_out5));  // open: en, clr
  Register sp (.D(WriteData), .Q(sp_q), .clk(demultiplexer_1_out6));  // open: en, clr
  Multiplexer #(.select(3), .width(8), .enable("false")) multiplexer_1 (
    .in0(zero_q), .in1(t0_q), .in2(t1_q), .in3(t2_q), .in4(t3_q), .in5(t4_q), .in6(sp_q), .out(ReadData1),
    .sel(RS[2:0]));  // open: in7
  Multiplexer #(.select(3), .width(8), .enable("false")) multiplexer_2 (
    .in0(zero_q), .in1(t0_q), .in2(t1_q), .in3(t2_q), .in4(t3_q), .in5(t4_q), .in6(sp_q), .out(ReadData2),
    .sel(RT[2:0]));  // open: in7
endmodule

module DataMemory (
  input  [7:0] Address,
  input  [7:0] WriteData,
  input  MemWrite,
  input  CLK,
  input  MemRead,
  output [7:0] ReadData
);

  RAM #(.bus("separate")) ram_1 (
    .addr(Address), .din(WriteData), .data(ReadData), .str(MemWrite), .clk(CLK), .ld(MemRead));  // open: sel, clr
endmodule

module ControlUnit (
  input  [3:0] OpCode,
  output out_2,
  output out_3,
  output out_4,
  output out_5,
  output out_6,
  output out_7,
  output out_8,
  output out_9,
  output [2:0] out_10
);

  ROM #(.addrWidth(4), .dataWidth(11)) rom_1 (
    .addr(OpCode), .data({out_10, out_9, out_8, out_7, out_6, out_5, out_4, out_3, out_2}));  // open: sel

  // Notes on the sheet:
  //   contents of rom_1 (hex, n*v repeats v):
  //   103 281 681 720 383 40 81 203 3 581 20 303 281 481 6 1b
endmodule
